# Fritzing sketch schematics_4digitDisplay (saved by Fritzing 0.9.3b)

parts:
  Raspberry_Pi_1 = Raspberry Pi 3 [part_number=RPI-3-V1.2]
  Grove1 = Grove 4 Digit Display

nets:
  N1: Raspberry_Pi_1.GPIO20, Grove1.CLK
  N2: Raspberry_Pi_1.GPIO16, Grove1.DIO
  GND: Raspberry_Pi_1.GND, Grove1.GND
  5V: Raspberry_Pi_1.5V, Grove1.VCC
