# Fritzing sketch schematics_color_led_touch_button (saved by Fritzing 0.9.3b)
breadboards: 1

parts:
  Raspberry_Pi_1 = Raspberry Pi 3 [part_number=RPI-3-V1.2]
  Sysolve_IoT2 = Touch Button
  R2 = Resistor [tolerance=±5% resistance=220 package=THT]
  R3 = Resistor [tolerance=±5% resistance=220 package=THT]
  R4 = Resistor [tolerance=±5% resistance=220 package=THT]
  LED3 = LED - 3mm [color="Green (555nm)" package="3 mm [THT]"]
  LED1 = LED - 3mm [color="Red (633nm)" package="3 mm [THT]"]
  LED2 = LED - 3mm [color="Blue (430nm)" package="3 mm [THT]"]

nets:
  3V3: Raspberry_Pi_1.3v3, Sysolve_IoT2.VCC
  GND: Raspberry_Pi_1.GND, Sysolve_IoT2.GND, LED3.cathode, LED1.cathode, LED2.cathode
  N1: Raspberry_Pi_1.GIPO13, R4.Pin_1
  N2: Raspberry_Pi_1.GIPO19, R2.Pin_0
  N3: Raspberry_Pi_1.GIPO21, Sysolve_IoT2.SIG
  N4: Raspberry_Pi_1.GIPO18, R3.Pin_1
  N5: R2.Pin_1, LED2.anode
  N6: R3.Pin_0, LED1.anode
  N7: R4.Pin_0, LED3.anode

custom parts:
  Touch Button: Sysolve Touch Button
