# Fritzing sketch schematics_oled (saved by Fritzing 0.9.3b)

parts:
  Raspberry_Pi_1 = Raspberry Pi 3 [part_number=RPI-3-V1.2]
  Sysolve_IoT1 = OLED 0.96" 128x64 I2C SSD1306

nets:
  N1: Raspberry_Pi_1.GPIO2, Sysolve_IoT1.SCA
  N2: Raspberry_Pi_1.GPIO3, Sysolve_IoT1.SCL
  GND: Raspberry_Pi_1.GND, Sysolve_IoT1.GND
  5V: Raspberry_Pi_1.5V, Sysolve_IoT1.VCC
